// Logisim project zad1.circ as structural Verilog: 1 circuit, main circuit main
module main (
  input  A,
  input  A_2,
  input  B,
  input  A_3,
  input  B_2,
  output out_6,
  output out_7,
  output out_8
);

  wire nor_1_out, nor_2_out, OR_out;

  not nor_1 (nor_1_out, A_2);  // NOR_Gate
  not nor_2 (nor_2_out, B);  // NOR_Gate
  nor OR (OR_out, A_3, B_2);
  not Not (out_6, A);  // NOR_Gate
  nor AND_star (out_7, nor_1_out, nor_2_out);
  not OR_plus (out_8, OR_out);  // NOR_Gate
endmodule
