// Logisim project zad2.circ as structural Verilog: 1 circuit, main circuit main
module main (
  input  A,
  input  B,
  input  C,
  input  A_2,
  input  B_2,
  input  C_2,
  output out_7,
  output out_8
);

  wire and_1_out, and_2_out, xnor_1_out, xor_1_out;

  and and_1 (and_1_out, A, ~B, C);  // AND_Gate
  and and_2 (and_2_out, ~A_2, ~B_2);  // AND_Gate
  NotExactlyOne xnor_1 (.out(xnor_1_out), .in0(A_2), .in2(B_2), .in4(C_2));
  xor xor_1 (xor_1_out, A, B);
  or or_1 (out_8, and_2_out, ~C_2, xnor_1_out);  // OR_Gate
  or or_2 (out_7, and_1_out, xor_1_out, C);
endmodule
