// Logisim project zad1 i zad2(DNF i CNF).circ as structural Verilog: 1 circuit, main circuit main
// A
module main (
  input  A,
  input  B,
  input  C,
  input  in_4,
  input  in_5,
  input  in_6,
  output out_7,
  output out_8
);

  wire nand_1_out, nand_2_out, nand_3_out, nand_4_out, nand_5_out, nand_6_out, nand_7_out, nor_1_out,
       nor_2_out, nor_3_out, nor_4_out, nor_5_out, nor_6_out, nor_7_out;

  not nand_1 (nand_1_out, A);  // NAND_Gate
  not nand_2 (nand_2_out, B);  // NAND_Gate
  not nand_3 (nand_3_out, C);  // NAND_Gate
  not nor_1 (nor_1_out, in_4);  // NOR_Gate
  not nor_2 (nor_2_out, in_5);  // NOR_Gate
  not nor_3 (nor_3_out, in_6);  // NOR_Gate
  nor nor_4 (nor_4_out, in_4, nor_2_out, in_6);
  nor nor_5 (nor_5_out, nor_1_out, in_5, in_6);
  nor nor_6 (nor_6_out, nor_1_out, in_5, nor_3_out);
  nor nor_7 (nor_7_out, nor_1_out, nor_2_out, in_6);
  nand nand_4 (nand_4_out, nand_1_out, B, nand_3_out);
  nand nand_5 (nand_5_out, A, nand_2_out, nand_3_out);
  nand nand_6 (nand_6_out, A, nand_2_out, C);
  nand nand_7 (nand_7_out, A, B, nand_3_out);
  nand DNF (out_7, nand_4_out, nand_5_out, nand_6_out, nand_7_out);
  nor CNF (out_8, nor_4_out, nor_5_out, nor_6_out, nor_7_out);
endmodule
