// Logisim project zad1.circ as structural Verilog: 1 circuit, main circuit main
module main (
  input  A,
  input  B,
  input  C,
  output LW,
  output RW
);

  wire nor_1_out, nor_2_out, nor_3_out, nor_4_out, nor_5_out, nor_6_out, nor_7_out;

  not nor_1 (nor_1_out, B);  // NOR_Gate
  not nor_2 (nor_2_out, C);  // NOR_Gate
  nor nor_3 (nor_3_out, C, nor_1_out);
  nor nor_4 (nor_4_out, B, nor_2_out);
  nor nor_5 (nor_5_out, nor_2_out, A);
  nor nor_6 (nor_6_out, nor_1_out, nor_3_out, nor_2_out, nor_4_out);
  nor nor_7 (nor_7_out, nor_1_out, nor_5_out);
  not nor_8 (LW, nor_6_out);  // NOR_Gate
  not nor_9 (RW, nor_7_out);  // NOR_Gate
endmodule
