// Logisim project cw 9.circ as structural Verilog: 2 circuits, main circuit main
module main (
);

  wire clock_1_out;
  wire [3:0] counter_1_q;
  wire [6:0] rom_1_data;

  Clock clock_1 (.out(clock_1_out));
  Counter #(.width(4), .max('hf)) counter_1 (
    .count(clock_1_out), .Q(counter_1_q), .clk(clock_1_out));  // open: load, D, carry, clr
  ROM #(.addrWidth(4), .dataWidth(7)) rom_1 (.addr(counter_1_q), .data(rom_1_data));  // open: sel
  _7_Segment_Display u_7_segment_display_1 (
    .g(rom_1_data[6]), .f(rom_1_data[5]), .a(rom_1_data[0]), .b(rom_1_data[1]), .e(rom_1_data[4]),
    .d(rom_1_data[3]), .c(rom_1_data[2]));  // open: dp
endmodule

module m (
  input  in_1
);

  wire and_1_out, and_2_out, clock_1_out, clock_2_out;
  wire [1:0] counter_1_q;
  wire [2:0] rom_1_data;

  Clock clock_1 (.out(clock_1_out));
  Clock #(.highDuration(4), .lowDuration(4)) clock_2 (.out(clock_2_out));
  Counter #(.width(2), .max('h3)) counter_1 (
    .Q(counter_1_q), .clk(clock_2_out), .clr(in_1));  // open: load, D, count, carry
  and and_1 (and_1_out, clock_1_out, in_1);
  ROM #(.addrWidth(2), .dataWidth(3)) rom_1 (.addr(counter_1_q), .data(rom_1_data));  // open: sel
  LED led_1 (.in(rom_1_data[0]));
  and and_2 (and_2_out, rom_1_data[1], ~and_1_out);  // AND_Gate
  LED led_2 (.in(and_2_out));
  LED led_3 (.in(rom_1_data[2]));
endmodule
