// Logisim project zd 123.circ as structural Verilog: 3 circuits, main circuit main
module main (
  input  in_1,
  input  in_2,
  input  in_3,
  input  in_4,
  output out_5,
  output out_6
);

  wire not_1_out;

  Multiplexer #(.select(4)) multiplexer_1 (
    .in0(1'b0), .in1(1'b0), .in2(1'b1), .in3(1'b0), .in4(1'b1), .in5(1'b0), .in6(1'b0), .in7(1'b1),
    .in8(1'b1), .in9(1'b0), .in10(1'b0), .in11(1'b1), .in12(1'b0), .in13(1'b1), .in14(1'b0), .in15(1'b1),
    .out(out_6), .sel({in_1, in_2, in_3, in_4}));  // open: en
  not not_1 (not_1_out, in_1);
  Multiplexer #(.select(3)) multiplexer_2 (
    .in0(in_1), .in1(1'b0), .in2(not_1_out), .in3(in_1), .in4(not_1_out), .in5(in_1), .in6(1'b0), .in7(1'b1),
    .out(out_5), .sel({in_2, in_3, in_4}));  // open: en
endmodule

module main3 (
  input  _3,
  input  _2,
  input  _1,
  input  _0,
  output out_5
);

  wire nand_1_out, nand_2_out, nand_3_out, nand_4_out, nand_5_out, nand_6_out, nand_7_out, nand_8_out,
       nand_9_out;

  nand nand_1 (nand_1_out, _3, _3);
  nand nand_2 (nand_2_out, _2, _2);
  nand nand_3 (nand_3_out, _3, _2);
  nand nand_4 (nand_4_out, nand_1_out, _2);
  nand nand_5 (nand_5_out, _3, nand_2_out);
  nand nand_6 (nand_6_out, nand_3_out, nand_3_out);
  nand nand_7 (nand_7_out, nand_1_out, nand_2_out);
  nand nand_8 (nand_8_out, nand_4_out, nand_5_out);
  nand nand_9 (nand_9_out, nand_7_out, nand_7_out);
  Multiplexer #(.select(2)) multiplexer_1 (
    .in0(nand_6_out), .in1(nand_8_out), .in2(nand_9_out), .in3(nand_7_out), .out(out_5), .sel({_1, _0}));  // open: en
endmodule

module m (
  input  a,
  input  b,
  output x
);


  assign x = a;
endmodule
