// Logisim project zad 1 2.circ as structural Verilog: 2 circuits, main circuit main
module main (
  input  [3:0] in_1,
  input  [3:0] in_2,
  output out_3,
  output out_4,
  output out_5,
  output out_6,
  output out_7,
  output out_8
);

  wire adder_1_cout, adder_2_cout, adder_3_cout;

  Adder #(.width(1)) adder_1 (.a(in_1[0]), .b(in_2[0]), .out(out_3), .cout(adder_1_cout));  // open: cin
  Adder #(.width(1)) adder_2 (.a(in_1[1]), .b(in_2[1]), .out(out_4), .cin(adder_1_cout), .cout(adder_2_cout));
  Adder #(.width(1)) adder_3 (.a(in_1[2]), .b(in_2[2]), .out(out_5), .cin(adder_2_cout), .cout(adder_3_cout));
  Adder #(.width(1)) adder_4 (.a(in_1[3]), .b(in_2[3]), .out(out_7), .cin(adder_3_cout), .cout(out_8));
  xor xor_1 (out_6, adder_3_cout, out_8);
endmodule

module zad2 (
  input  [3:0] in_1,
  input  [3:0] in_2,
  input  in_3,
  input  in_4,
  output out_5,
  output out_6,
  output out_7,
  output out_8,
  output out_9,
  output out_10,
  output out_11
);

  wire adder_1_cout, adder_2_cout, adder_3_cout;
  wire [3:0] adder_1_out, and_1_out, negator_1_out, xor_1_out;

  Negator #(.width(4)) negator_1 (.in(in_1), .out(negator_1_out));
  assign xor_1_out = in_1 ^ in_2;  // XOR_Gate xor_1, 4 bits wide
  assign and_1_out = in_1 & in_2;  // AND_Gate and_1, 4 bits wide
  Adder #(.width(1)) adder_1 (.a(in_1[0]), .b(in_2[0]), .out(adder_1_out[0]), .cout(adder_1_cout));  // open: cin
  Adder #(.width(1)) adder_2 (.a(in_1[1]), .b(in_2[1]), .out(adder_1_out[1]), .cin(adder_1_cout), .cout(adder_2_cout));
  Adder #(.width(1)) adder_3 (.a(in_1[2]), .b(in_2[2]), .out(adder_1_out[2]), .cin(adder_2_cout), .cout(adder_3_cout));
  Adder #(.width(1)) adder_4 (.a(in_1[3]), .b(in_2[3]), .out(adder_1_out[3]), .cin(adder_3_cout), .cout(out_11));
  Multiplexer #(.select(2), .width(4)) multiplexer_1 (
    .in0(negator_1_out), .in1(xor_1_out), .in2(and_1_out), .in3(adder_1_out),
    .out({out_6, out_7, out_8, out_9}), .sel({in_3, in_4}));  // open: en
  xor xor_2 (out_10, adder_3_cout, out_11);
  nor nor_1 (out_5, out_6, out_7, out_8, out_9);
endmodule
