// Logisim project zad 2,3.circ as structural Verilog: 2 circuits, main circuit main
module main (
  input  [3:0] in_1,
  input  [3:0] in_2,
  input  [3:0] in_3,
  input  [3:0] in_4,
  input  [3:0] in_5
);

  wire and_1_out, clock_1_out, d_ff_1_qn, d_ff_2_qn, d_ff_3_qn, d_ff_4_qn;
  wire [3:0] d_ff_1_q, multiplexer_1_out, multiplexer_2_out;

  Clock clock_1 (.out(clock_1_out));
  D_Flip_Flop d_ff_1 (
    .clk(clock_1_out), .D(d_ff_1_qn), .Q(d_ff_1_q[0]), .Qn(d_ff_1_qn), .reset(and_1_out));  // open: preset, en
  D_Flip_Flop d_ff_2 (
    .clk(d_ff_1_qn), .D(d_ff_2_qn), .Q(d_ff_1_q[1]), .Qn(d_ff_2_qn), .reset(and_1_out));  // open: preset, en
  D_Flip_Flop d_ff_3 (
    .clk(d_ff_2_qn), .D(d_ff_3_qn), .Q(d_ff_1_q[2]), .Qn(d_ff_3_qn), .reset(and_1_out));  // open: preset, en
  D_Flip_Flop d_ff_4 (
    .clk(d_ff_3_qn), .D(d_ff_4_qn), .Q(d_ff_1_q[3]), .Qn(d_ff_4_qn), .reset(and_1_out));  // open: preset, en
  and and_1 (and_1_out, d_ff_1_q[2], d_ff_1_q[1], d_ff_1_q[0], d_ff_1_q[3]);
  Multiplexer #(.select(4), .width(4)) multiplexer_1 (
    .in0(4'b0000), .in1(4'b0000), .in2(4'b0000), .in3(4'b0000), .in4(d_ff_1_q), .in5(d_ff_1_q),
    .in6(d_ff_1_q), .in7(d_ff_1_q), .in8(d_ff_1_q), .in9(d_ff_1_q), .in10(4'b0000), .in11(in_1), .in12(in_2),
    .in13(in_3), .in14(in_4), .in15(4'b0000), .out(multiplexer_1_out), .sel(d_ff_1_q));  // open: en
  Hex_Digit_Display hex_digit_display_1 (.value(multiplexer_2_out));  // open: dp
  Multiplexer #(.select(4), .width(4)) multiplexer_2 (
    .in0(4'b0000), .in1(4'b0000), .in2(4'b0000), .in3(4'b0000), .in4(4'b0000), .in5(4'b0000), .in6(4'b0000),
    .in7(4'b0000), .in8(4'b0000), .in9(4'b0000), .in10(in_5), .in11(in_5), .in12(in_5), .in13(in_5),
    .in14(in_5), .in15(in_5), .out(multiplexer_2_out), .sel(d_ff_1_q));  // open: en
  Hex_Digit_Display hex_digit_display_2 (.value(multiplexer_1_out));  // open: dp
endmodule

module main2 (
  input  in_1
);

  wire clock_1_out, xor_1_out;
  wire [3:0] d_ff_1_q;

  Clock clock_1 (.out(clock_1_out));
  D_Flip_Flop d_ff_1 (.clk(clock_1_out), .D(xor_1_out), .Q(d_ff_1_q[0]), .preset(in_1));  // open: Qn, en, reset
  D_Flip_Flop d_ff_2 (.clk(clock_1_out), .D(d_ff_1_q[0]), .Q(d_ff_1_q[1]), .preset(in_1));  // open: Qn, en, reset
  xor xor_1 (xor_1_out, d_ff_1_q[3], d_ff_1_q[2]);
  D_Flip_Flop d_ff_3 (.clk(clock_1_out), .D(d_ff_1_q[1]), .Q(d_ff_1_q[2]), .preset(in_1));  // open: Qn, en, reset
  D_Flip_Flop d_ff_4 (.clk(clock_1_out), .D(d_ff_1_q[2]), .Q(d_ff_1_q[3]), .preset(in_1));  // open: Qn, en, reset
  Hex_Digit_Display hex_digit_display_1 (.value(d_ff_1_q));  // open: dp
endmodule
