// Logisim project cw8.circ as structural Verilog: 1 circuit, main circuit m
module m (
  input  in_1,
  input  in_2
);

  wire and_1_out, and_2_out, and_3_out, and_4_out, clock_1_out, d_ff_1_q, d_ff_2_q, nand_1_out, not_1_out,
       not_2_out, not_3_out, not_4_out, or_1_out, or_2_out, shift_register_1_out, xor_1_out;

  Clock clock_1 (.out(clock_1_out));
  Shift_Register shift_register_1 (
    .shift(in_2), .in(in_1), .clk(clock_1_out), .out(shift_register_1_out), .load(d_ff_1_q),
    .clr(shift_register_1_out), .d0(d_ff_1_q), .d1(d_ff_1_q), .d2(d_ff_1_q), .d3(d_ff_1_q), .d4(d_ff_1_q),
    .d5(d_ff_1_q), .d6(d_ff_1_q), .d7(d_ff_1_q));  // open: q0, q1, q2, q3, q4, q5, q6, q7
  nand nand_1 (nand_1_out, in_2, d_ff_1_q);
  not not_1 (not_1_out, in_2);
  xor xor_1 (xor_1_out, d_ff_1_q, d_ff_2_q);
  not not_2 (not_2_out, in_2);
  or or_1 (or_1_out, not_1_out, xor_1_out);
  and and_1 (and_1_out, not_2_out, clock_1_out);
  D_Flip_Flop d_ff_1 (.clk(shift_register_1_out), .D(nand_1_out), .Q(d_ff_1_q));  // open: Qn, preset, en, reset
  D_Flip_Flop d_ff_2 (.clk(shift_register_1_out), .D(or_1_out), .Q(d_ff_2_q));  // open: Qn, preset, en, reset
  not not_3 (not_3_out, d_ff_1_q);
  not not_4 (not_4_out, d_ff_2_q);
  and and_2 (and_2_out, d_ff_2_q, not_3_out);
  and and_3 (and_3_out, in_2, not_4_out);
  LED led_1 (.in(and_3_out));
  or or_2 (or_2_out, and_1_out, d_ff_1_q);
  LED led_2 (.in(or_2_out));
  LED led_3 (.in(and_4_out));
  and and_4 (and_4_out, and_2_out, in_2);
endmodule
